# Fritzing sketch AlarmClock (saved by Fritzing 1.0.2b)
breadboards: 1

parts:
  Part1 = LCD1602-I2C
  Q1 = PNP-Transistor [package="TO92 [THT]"]
  LED1 = LED - 5mm [color="Red (633nm)" current=0.030A package="5 mm [THT]"]
  Active_Buzzer = Piezo Buzzer
  LED2 = LED - 5mm [color="Green (555nm)" current=0.030A package="5 mm [THT]"]
  R1 = Resistor [tolerance=±5% resistance=1k package="0603 [SMD]"]
  Keypad4x2 = Keypad Membran 4x4
  J2 = Raspberry Pi Header 40pin [package=THT]
  R2 = Resistor [tolerance=±5% resistance=220 package="0603 [SMD]"]
  R3 = Resistor [tolerance=±5% resistance=220 package="0603 [SMD]"]
  R4 = Resistor [tolerance=±5% resistance=10k package="0603 [SMD]"]
  R5 = Resistor [tolerance=±5% resistance=10k package="0603 [SMD]"]
  R6 = Resistor [tolerance=±5% resistance=10k package="0603 [SMD]"]
  R7 = Resistor [tolerance=±5% resistance=10k package="0603 [SMD]"]

nets:
  GND: Part1.GND, Q1.C, LED1.cathode, LED2.cathode, J2.GND
  VCC: Part1.VCC, J2.5V
  N1: Part1.SDA, J2.GPIO2
  N2: Part1.SCL, J2.IO3
  N3: Q1.E, Active_Buzzer.pin_2
  N4: Q1.B, R1.Pin_1
  N5: LED1.anode, R3.Pin_1
  N6: Active_Buzzer.pin_1, J2.3V3, R4.Pin_1, R5.Pin_1, R6.Pin_1, R7.Pin_1
  N7: LED2.anode, R2.Pin_1
  N8: R1.Pin_0, J2.IO21
  N9: Keypad4x2.Pin1, J2.IO18, R4.Pin_0
  N10: Keypad4x2.Pin2, J2.IO23, R5.Pin_0
  N11: Keypad4x2.Pin3, J2.IO24, R7.Pin_0
  N12: Keypad4x2.Pin4, J2.IO25, R6.Pin_0
  N13: Keypad4x2.Pin5, J2.IO10
  N14: Keypad4x2.Pin6, J2.IO22#14
  N15: Keypad4x2.Pin7, J2.IO22#12
  N16: Keypad4x2.Pin8, J2.IO17
  N17: J2.IO19, R2.Pin_0
  N18: J2.IO26, R3.Pin_0

custom parts:
  LCD1602-I2C: A standard character display, usually with 2x16 characters. Comes in many colors with LCM1602 IIC attached.
  Piezo Buzzer: Part from https://www.nutsvolts.com/magazine/article/november2012_SmileysWorkshop. Breadboard and icon images modified to be 0.3" in spacing and be more similar to the actual physical part.
  Keypad Membran 4x4: Membrane Keypad 4x4 Matrix
  Raspberry Pi Header 40pin: Raspberry Pi 40 pin header - for creating your own shields. (Mar 2020, bb: make breadboard friendly (.4in pin spacing) and add labels. Schematic add labels. PCB make oblong pins to allow routing traces between the pins.)
